# Fritzing sketch DMN_Version_1.5 (saved by Fritzing 0.9.3b)
breadboards: 5

parts:
  Raspberry_Pi_1 = Raspberry Pi 3 [part_number=RPI-3-V1.2]
  M1 = 1 chan 5v relay module
  VCC1 = Battery
  L1 = Solenoid
  LED7 = smd LED [color="Red (633nm)" package="0805 [SMD]"]
  LED8 = smd LED [color="Green (565nm)" package="0805 [SMD]"]
  R7 = Resistor [tolerance=±5% resistance=68 package=THT]
  R8 = Resistor [tolerance=±5% resistance=68 package=THT]
  R9 = Resistor [tolerance=±5% resistance=68 package=THT]
  LED9 = smd LED [color="Red (633nm)" package="0805 [SMD]"]
  R10 = Resistor [tolerance=±5% resistance=68 package=THT]
  LED10 = smd LED [color="Green (565nm)" package="0805 [SMD]"]
  LED11 = smd LED [color="Red (633nm)" package="0805 [SMD]"]
  LED12 = smd LED [color="Green (565nm)" package="0805 [SMD]"]
  R11 = Resistor [tolerance=±5% resistance=68 package=THT]
  R12 = Resistor [tolerance=±5% resistance=68 package=THT]
  J1 = Piezo Speaker
  R13 = Resistor [tolerance=±5% resistance=220 package=THT]
  S1 = Momentary Switch [package=ksa_sealed_tac_switch]
  R14 = Resistor [tolerance=±5% resistance=1k package=THT]
  PIR1 = PIR sensor

nets:
  3V3: Raspberry_Pi_1.3v3, Raspberry_Pi_1.3V3, M1.pin_1, S1.3
  N1: Raspberry_Pi_1.GPIO2, R12.Pin_0
  N2: Raspberry_Pi_1.GPIO3, R11.Pin_0
  N3: Raspberry_Pi_1.GIPO27, PIR1.SIG
  N4: Raspberry_Pi_1.GIPO11, R10.Pin_0
  N5: Raspberry_Pi_1.GIPO19, R14.Pin_1
  N6: Raspberry_Pi_1.GIPO26, R9.Pin_0
  GND: Raspberry_Pi_1.GND, M1.pin_2, LED7.cathode, LED8.cathode, LED9.cathode, LED10.cathode, LED11.cathode, LED12.cathode, J1.pin1, PIR1.GND
  N7: Raspberry_Pi_1.GIPO21, R13.Pin_0
  N8: Raspberry_Pi_1.GIPO16, R7.Pin_0
  N9: Raspberry_Pi_1.GIPO12, R8.Pin_0
  N10: Raspberry_Pi_1.GIPO18, M1.pin_3
  5V: Raspberry_Pi_1.5V, PIR1.VDD
  N11: M1.pin_4, VCC1.+
  N12: M1.pin_5, L1.pin2
  N13: LED7.anode, R7.Pin_1
  N14: LED8.anode, R8.Pin_1
  N15: R9.Pin_1, LED9.anode
  N16: R10.Pin_1, LED10.anode
  N17: LED11.anode, R11.Pin_1
  N18: LED12.anode, R12.Pin_1
  N19: J1.pin2, R13.Pin_1
  N20: S1.1, R14.Pin_0

notes:
  Plug camera into camera port
  Plug official power supply
  Connect speaker via aux cable
  5v relay single channel relay
  Connect finger scanner via uart USB attachment
  Piezo buzzer, 220 ohm resistor
  momentary switch, connected to 3.3v power, 1 Kilo ohm resistor, connected to gpio, Responsible for input from user
  Another switch like this will be used as a door closed/opened state keeper, unfortunately this will not fit on this pi as is, more than one pi will likely be needed due to the 3.3v rail being constrained to 50mA
  In the real version, a 12v dc power supply is used
  12v sub-600 mA electric strike lock
  PIR sensor
  2.2v LEDs with 68 ohm resistors

custom parts:
  1 chan 5v relay module: 1 Channel 5V Relay Module Board Shield with Optocoupler Support High and Low Level Trigger for Arduino.
