# Fritzing sketch Untitled Sketch 4 (saved by Fritzing 0.9.3b)
breadboards: 1

parts:
  Part1 = Arduino Uno (Rev3)
  S1 = Pushbutton [package="[THT]"]
  R1 = Resistor [tolerance=±5% resistance=10k package=THT]
  LED1 = LED - 5mm [color="Red (633nm)" package="5 mm [THT]"]
  R2 = Resistor [tolerance=±5% resistance=150 package=THT]
  LED2 = LED - 5mm [color="Green (565nm)" package="5 mm [THT]"]
  R3 = Resistor [tolerance=±5% resistance=150 package=THT]
  Mod1 = KY-016 RGB Full Color LED Module [package="Breakout board"]
  J1 = Basic Servo
  VCC2 = Battery  # not connected
  X1 = USB Connectors [package=usb-minib-nostop]  # not connected

nets:
  N1: Part1.D9_PWM, Mod1.B
  N2: Part1.D10_PWM/SS, Mod1.G
  N3: Part1.D11_PWM/MOSI, Mod1.R
  N4: Part1.D12/MISO, S1.Pin_1, S1.Pin_2, R1.Pin_1
  N5: Part1.D13/SCK, LED1.anode
  N6: Part1.D6_PWM, J1.pulse
  5V: Part1.5V, S1.Pin_3, S1.Pin_4, J1.vcc
  GND: Part1.GND, R1.Pin_0, R2.Pin_0, R3.Pin_0, Mod1.-, J1.gnd
  N7: LED1.cathode, R2.Pin_1
  N8: LED2.cathode, R3.Pin_1

custom parts:
  KY-016 RGB Full Color LED Module: KY-016 Arduino full color 5mm RGB LED, different colors can be obtained by mixing the three primary colors.
